# Fritzing sketch Untitled Sketch (saved by Fritzing 0.9.10b)
circuit board: 10.1372cm x 5.54968cm
breadboards: 1

parts:
  S1 = Pushbutton [package="[THT]"]
  S3 = Pushbutton [package="[THT]"]
  S4 = Pushbutton [package="[THT]"]
  R2 = Resistor [tolerance=±5% power=0.25 resistance=220 package=THT]
  R3 = Resistor [tolerance=±5% power=0.25 resistance=220 package=THT]
  R4 = Resistor [tolerance=±5% power=0.25 resistance=220 package=THT]
  LED2 = RGB LED (com. cathode, rgb) [package="5 mm [THT]"]
  元件1 = Arduino Mega 2560 (Rev3) [part_number=lcd]
  R5 = Resistor [tolerance=±5% power=0.25 resistance=220 package=THT]
  R6 = Resistor [tolerance=±5% power=0.25 resistance=220 package=THT]
  R7 = Resistor [tolerance=±5% power=0.25 resistance=220 package=THT]
  R1_220Ohm = Resistor [tolerance=±5% power=0.25 resistance=220 package=THT]
  S5 = Toggle Switch [package=THT]
  R8 = Resistor [tolerance=±5% power=0.25 resistance=220 package=THT]
  S2 = Pushbutton [package="[THT]"]
  power6v = Screw terminal - 2 pins [package=THT]
  J2 = Basic Servo
  J3 = Basic Servo
  gyro = Grove OLED 128x96 [part_number=lcd]
  lcd = Grove 3 Axis Digital Accelerometer 16g

nets:
  5V: S1.Pin_1, S1.Pin_2, S3.Pin_1, S3.Pin_2, S4.Pin_1, S4.Pin_2, R2.Pin_1, R3.Pin_1, R4.Pin_1, 元件1.5V, 元件1.D2_PWM, 元件1.D3_PWM, 元件1.D4_PWM, 元件1.D5_PWM, R1_220Ohm.Pin_1, S5.COM, S2.Pin_1, S2.Pin_2, lcd.VCC
  GND: R2.Pin_0, R3.Pin_0, R4.Pin_0, LED2.common_cathode, 元件1.GND, R1_220Ohm.Pin_0, R8.Pin_0, power6v.pin1, J2.gnd, J3.gnd, gyro.GND, lcd.GND
  N1: LED2.red_anode, R5.Pin_1
  N2: LED2.green_anode, R6.Pin_1
  N3: LED2.blue_anode, R7.Pin_1
  N4: 元件1.D21/SCL, 元件1.SCL, lcd.SCL
  N5: 元件1.D20/SDA, 元件1.SDA, lcd.SDA
  N6: 元件1.D13_PWM, R7.Pin_0
  N7: 元件1.D12_PWM, R6.Pin_0
  N8: 元件1.D11_PWM, R5.Pin_0
  N9: 元件1.D10_PWM, J2.pulse
  N10: 元件1.D9_PWM, J3.pulse
  3V3: 元件1.3V3, gyro.VCC
  N11: 元件1.D1_TX0, S5.L1, R8.Pin_1
  VCC: power6v.pin2, J2.vcc, J3.vcc

notes:
  5v
  GND
  scl-sda
  R GR G B
  6v
